// Logisim project Semaforo.circ as structural Verilog: 4 circuits, main circuit RL Completo
module RL_Transiozioni (
  input  x1,
  input  x0,
  input  a,
  input  b,
  input  c,
  output Y2,
  output Y1,
  output Y0
);

  wire and_1_out, and_2_out, and_3_out, and_4_out, and_5_out, and_6_out, and_7_out, and_8_out, and_9_out,
       not_1_out, not_2_out, not_3_out, not_4_out, not_5_out, not_6_out, not_7_out, not_8_out, not_9_out,
       not_10_out, not_11_out, not_12_out, not_13_out, not_14_out, not_15_out, not_16_out, not_17_out,
       not_18_out;

  not not_1 (not_1_out, c);
  not not_2 (not_2_out, c);
  not not_3 (not_3_out, x1);
  not not_4 (not_4_out, a);
  not not_5 (not_5_out, b);
  not not_6 (not_6_out, x1);
  not not_7 (not_7_out, a);
  not not_8 (not_8_out, c);
  not not_9 (not_9_out, x0);
  not not_10 (not_10_out, a);
  not not_11 (not_11_out, b);
  not not_12 (not_12_out, a);
  not not_13 (not_13_out, c);
  not not_14 (not_14_out, x0);
  not not_15 (not_15_out, b);
  not not_16 (not_16_out, c);
  not not_17 (not_17_out, a);
  not not_18 (not_18_out, b);
  and and_1 (and_1_out, b, c);
  and and_2 (and_2_out, a, not_1_out);
  and and_3 (and_3_out, b, not_2_out);
  and and_4 (and_4_out, not_3_out, x0, not_4_out, not_5_out, c);
  and and_5 (and_5_out, not_6_out, not_7_out, not_8_out);
  and and_6 (and_6_out, not_9_out, not_10_out, not_11_out);
  and and_7 (and_7_out, x0, not_12_out, not_13_out);
  and and_8 (and_8_out, x1, not_14_out, not_15_out, not_16_out);
  and and_9 (and_9_out, x1, not_17_out, not_18_out);
  or or_1 (Y2, and_1_out, and_2_out);
  or or_2 (Y1, and_3_out, and_4_out);
  or or_3 (Y0, and_5_out, and_6_out, and_7_out, and_8_out, and_9_out);
endmodule

module RL_Uscite (
  input  x1,
  input  x0,
  input  y2,
  input  y1,
  input  y0,
  output z1,
  output z0
);

  wire and_1_out, and_2_out, and_3_out, not_1_out, not_2_out, not_3_out, not_4_out, not_5_out, not_6_out;

  not not_1 (not_1_out, y0);
  not not_2 (not_2_out, x1);
  not not_3 (not_3_out, y2);
  not not_4 (not_4_out, y1);
  not not_5 (not_5_out, x0);
  not not_6 (not_6_out, y0);
  and and_1 (and_1_out, y2, not_1_out);
  and and_2 (and_2_out, not_2_out, x0, not_3_out, not_4_out, y0);
  and and_3 (and_3_out, x1, not_5_out, y2, not_6_out);
  or or_1 (z1, y1, and_1_out);
  or or_2 (z0, and_2_out, and_3_out);
endmodule

module RL_Completo (
  input  x1,
  input  x0,
  output Y2,
  output Y1,
  output Y0,
  output z1,
  output z0
);

  wire and_1_out, and_2_out, and_3_out, and_4_out, and_5_out, and_6_out, and_7_out, and_8_out, and_9_out,
       and_10_out, and_11_out, and_12_out, and_13_out, and_14_out, and_15_out, and_16_out, clock_1_out,
       d_ff_1_q, d_ff_2_q, d_ff_3_q, not_1_out, not_2_out, not_3_out, not_4_out, not_5_out, not_6_out,
       not_7_out, not_8_out, not_9_out, not_10_out, not_11_out, not_12_out, not_13_out, not_14_out,
       not_15_out, not_16_out, not_17_out, not_18_out, not_19_out, not_20_out, not_21_out, not_22_out,
       not_23_out, not_24_out, not_25_out, not_26_out, not_27_out;

  not not_1 (not_1_out, d_ff_3_q);
  not not_2 (not_2_out, x1);
  not not_3 (not_3_out, d_ff_1_q);
  not not_4 (not_4_out, d_ff_2_q);
  not not_5 (not_5_out, x0);
  not not_6 (not_6_out, d_ff_3_q);
  not not_7 (not_7_out, d_ff_3_q);
  not not_8 (not_8_out, d_ff_3_q);
  not not_9 (not_9_out, x1);
  not not_10 (not_10_out, d_ff_1_q);
  not not_11 (not_11_out, d_ff_2_q);
  not not_12 (not_12_out, x1);
  not not_13 (not_13_out, d_ff_1_q);
  not not_14 (not_14_out, d_ff_3_q);
  not not_15 (not_15_out, x0);
  not not_16 (not_16_out, d_ff_1_q);
  not not_17 (not_17_out, d_ff_2_q);
  not not_18 (not_18_out, d_ff_1_q);
  not not_19 (not_19_out, d_ff_3_q);
  not not_20 (not_20_out, x0);
  not not_21 (not_21_out, d_ff_2_q);
  not not_22 (not_22_out, d_ff_3_q);
  not not_23 (not_23_out, d_ff_1_q);
  not not_24 (not_24_out, d_ff_2_q);
  and and_1 (and_1_out, d_ff_1_q, not_1_out);
  and and_2 (and_2_out, not_2_out, x0, not_3_out, not_4_out, d_ff_3_q);
  and and_3 (and_3_out, x1, not_5_out, d_ff_1_q, not_6_out);
  and and_4 (and_4_out, d_ff_2_q, d_ff_3_q);
  and and_5 (and_5_out, d_ff_1_q, not_7_out);
  and and_6 (and_6_out, d_ff_2_q, not_8_out);
  and and_7 (and_7_out, not_9_out, x0, not_10_out, not_11_out, d_ff_3_q);
  and and_8 (and_8_out, not_12_out, not_13_out, not_14_out);
  and and_9 (and_9_out, not_15_out, not_16_out, not_17_out);
  and and_10 (and_10_out, x0, not_18_out, not_19_out);
  and and_11 (and_11_out, x1, not_20_out, not_21_out, not_22_out);
  and and_12 (and_12_out, x1, not_23_out, not_24_out);
  or or_1 (z1, d_ff_2_q, and_1_out);
  or or_2 (z0, and_2_out, and_3_out);
  or or_3 (Y2, and_4_out, and_5_out);
  or or_4 (Y1, and_6_out, and_7_out);
  or or_5 (Y0, and_8_out, and_9_out, and_10_out, and_11_out, and_12_out);
  Clock clock_1 (.out(clock_1_out));
  not not_25 (not_25_out, z1);
  not not_26 (not_26_out, z0);
  not not_27 (not_27_out, z0);
  D_Flip_Flop d_ff_1 (.clk(clock_1_out), .D(Y2), .Q(d_ff_1_q));  // open: Qn, preset, en, reset
  D_Flip_Flop d_ff_2 (.clk(clock_1_out), .D(Y1), .Q(d_ff_2_q));  // open: Qn, preset, en, reset
  and and_13 (and_13_out, not_25_out, z0);
  and and_14 (and_14_out, not_25_out, not_26_out);
  and and_15 (and_15_out, z0, z1);
  and and_16 (and_16_out, not_27_out, z1);
  D_Flip_Flop d_ff_3 (.clk(clock_1_out), .D(Y0), .Q(d_ff_3_q));  // open: Qn, preset, en, reset
  LED led_1 (.in(z1));
  LED led_2 (.in(and_13_out));
  LED led_3 (.in(and_14_out));
  LED led_4 (.in(not_25_out));
  LED led_5 (.in(and_15_out));
  LED led_6 (.in(and_16_out));

  // Notes on the sheet:
  //   y2
  //   y1
  //   y0
  //   x1
  //   x0
  //   y2
  //   y1
  //   y0
  //   semaforo EW
  //   semaforo NS
endmodule

module RL_Sintetizzato (
  input  z1,
  input  z0,
  output z1_2,
  output z0_2
);

  wire and_1_out, and_2_out, and_3_out, and_4_out, clock_1_out, not_1_out, not_2_out, not_3_out,
       R_L_Tabella_Transizioni_y0, R_L_Tabella_Transizioni_y1, R_L_Tabella_Transizioni_y2, y0_q, y1_q, y2_q;

  RL_Transiozioni R_L_Tabella_Transizioni (
    .x1(z1), .x0(z0), .a(y2_q), .b(y1_q), .c(y0_q), .Y2(R_L_Tabella_Transizioni_y2),
    .Y1(R_L_Tabella_Transizioni_y1), .Y0(R_L_Tabella_Transizioni_y0));
  RL_Uscite R_L_Tabella_delle_Uscite (.x1(z1), .x0(z0), .y2(y2_q), .y1(y1_q), .y0(y0_q), .z1(z1_2), .z0(z0_2));
  Clock clock_1 (.out(clock_1_out));
  D_Flip_Flop y2 (.clk(clock_1_out), .D(R_L_Tabella_Transizioni_y2), .Q(y2_q));  // open: Qn, preset, en, reset
  D_Flip_Flop y1 (.clk(clock_1_out), .D(R_L_Tabella_Transizioni_y1), .Q(y1_q));  // open: Qn, preset, en, reset
  D_Flip_Flop y0 (.clk(clock_1_out), .D(R_L_Tabella_Transizioni_y0), .Q(y0_q));  // open: Qn, preset, en, reset
  not not_1 (not_1_out, z1_2);
  not not_2 (not_2_out, z0_2);
  not not_3 (not_3_out, z0_2);
  and and_1 (and_1_out, not_1_out, z0_2);
  and and_2 (and_2_out, not_1_out, not_2_out);
  and and_3 (and_3_out, z0_2, z1_2);
  and and_4 (and_4_out, not_3_out, z1_2);
  LED led_1 (.in(z1_2));
  LED led_2 (.in(and_1_out));
  LED led_3 (.in(and_2_out));
  LED led_4 (.in(not_1_out));
  LED led_5 (.in(and_3_out));
  LED led_6 (.in(and_4_out));

  // Notes on the sheet:
  //   semaforo EW
  //   semaforo NS
endmodule
